# Fritzing sketch schematics (saved by Fritzing 1.0.4)
breadboards: 1

parts:
  A1 = ESP32 DevKitc V4
  Screw_Connector = Camdenboss CTB0158-6 [part_number=CTB0158-6 package=THT]
  SP1 = SPEAKER [package=pcb_mount_speaker]
  Doorbell_Switch = SWITCH-MOMENTARY-2 [package=tactile-switch-1101ne]
  Doorbell_LED = LEDs [package=led10mm]
  Screw_Connector_2 = Camdenboss CTB0158-6 [part_number=CTB0158-6 package=THT]
  HLK-PM1 = HLK-PM01
  Powerline = AC Power [voltage=230V frequency=50Hz]
  Bauteil1 = Adafruit MAX98357A I2S 3W Class D Amplifier [part_number="Adafruit #3006"]  # not connected
  Bauteil2 = Adafruit MAX98357A I2S 3W Class D Amplifier [part_number="Adafruit #3006"]

nets:
  N1: A1.Pin_7, Screw_Connector_2.pin3
  N2: A1.Pin_8, Screw_Connector_2.pin5
  N3: A1.Pin_9, Bauteil2.DIN
  N4: A1.Pin_10, Bauteil2.LRCLK
  N5: A1.Pin_11, Bauteil2.BCLK
  N6: A1.Pin_19, Screw_Connector_2.pin1, Bauteil2.VIN
  N7: A1.Pin_32, A1.Pin_38, Screw_Connector_2.pin2, Screw_Connector_2.pin4
  N8: Screw_Connector.pin5, Bauteil2.VO-
  N9: Screw_Connector.pin6, Bauteil2.VO+
  N10: Screw_Connector.terminal_5, SP1.-
  N11: Screw_Connector.terminal_6, SP1.+
  N12: Doorbell_Switch.1, Screw_Connector_2.terminal_5
  N13: Doorbell_Switch.2, Screw_Connector_2.terminal_6
  N14: Doorbell_LED.C, Screw_Connector_2.terminal_4
  N15: Doorbell_LED.A, Screw_Connector_2.terminal_3
  N16: Screw_Connector_2.terminal_1, HLK-PM1.+Vo
  N17: Screw_Connector_2.terminal_2, HLK-PM1.-Vo
  N18: HLK-PM1.AC#0, Powerline.V+
  N19: HLK-PM1.AC#1, Powerline.V-

notes:
  Power Supply can be any 5V supply for DIN hat rail mount

custom parts:
  ESP32 DevKitc V4: ESP32-DevKitC board with ESP32-WROOM-32 module. ESP32-DevKitC V4 is a small-sized ESP32-based development board produced by Espressif. Most of the pins on the ESP module are broken out to the pin headers on the board. The pins D0, D1, D2, D3, CMD and CLK are used internally for communication between ESP32 and SPI flash memory. They are grouped on both sides near the USB connector. Avoid using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
  Adafruit MAX98357A I2S 3W Class D Amplifier: Listen to this good news - we now have an all in one digital audio amp breakout board that works incredibly well with the Raspberry Pi! If you're looking for an easy and low cost way to get you digital sound files bumpin' then the MAX08357 I2S Amp Breakout is for you. It takes standard I2S digital audio input and, not only decodes it into analog, but also amplifies it directly into a speaker.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
